# Fritzing sketch PomodorIoT (saved by Fritzing 0.9.3b)
breadboards: 1

parts:
  R1 = Resistor [tolerance=±5% resistance=220 package=THT]
  LED1 = LED - 5mm [color="Yellow (595nm)" package="5 mm [THT]"]
  LED2 = LED - 5mm [color="Yellow (595nm)" package="5 mm [THT]"]
  LED3 = LED - 5mm [color="Yellow (595nm)" package="5 mm [THT]"]
  LED4 = LED - 5mm [color="Yellow (595nm)" package="5 mm [THT]"]
  LED5 = LED - 5mm [color="Green (570nm)" package="5 mm [THT]"]
  LED6 = LED - 5mm [color="Green (570nm)" package="5 mm [THT]"]
  LED7 = LED - 5mm [color="Green (570nm)" package="5 mm [THT]"]
  R3 = Resistor [tolerance=±5% resistance=220 package=THT]
  R4 = Resistor [tolerance=±5% resistance=220 package=THT]
  R5 = Resistor [tolerance=±5% resistance=220 package=THT]
  R6 = Resistor [tolerance=±5% resistance=220 package=THT]
  R7 = Resistor [tolerance=±5% resistance=220 package=THT]
  R8 = Resistor [tolerance=±5% resistance=220 package=THT]
  LED8 = LED - 5mm [color="Red (633nm)" package="5 mm [THT]"]
  R9 = Resistor [tolerance=±5% resistance=220 package=THT]
  Part1 = Arduino Uno (Rev3)
  S1 = Pushbutton [package="[THT]"]
  R10 = Resistor [tolerance=±5% resistance=10k package=THT]

nets:
  N1: R1.Pin_0, LED1.cathode
  N2: R1.Pin_1, R3.Pin_1, R4.Pin_1, R5.Pin_1, R6.Pin_1, R7.Pin_1, R8.Pin_1, R9.Pin_1, Part1.GND, R10.Pin_1
  N3: LED1.anode, Part1.D3_PWM
  N4: LED2.cathode, R4.Pin_0
  N5: LED2.anode, Part1.D5_PWM
  N6: LED3.cathode, R6.Pin_0
  N7: LED3.anode, Part1.D6_PWM
  N8: LED4.cathode, R7.Pin_0
  N9: LED4.anode, Part1.D9_PWM
  N10: LED5.cathode, R9.Pin_0
  N11: LED5.anode, Part1.D7
  N12: LED6.cathode, R5.Pin_0
  N13: LED6.anode, Part1.D4
  N14: LED7.cathode, R3.Pin_0
  N15: LED7.anode, Part1.D8
  N16: R8.Pin_0, LED8.cathode
  N17: LED8.anode, Part1.D13/SCK
  N18: Part1.D2, S1.Pin_3, S1.Pin_4, R10.Pin_0
  N19: Part1.5V, S1.Pin_1, S1.Pin_2
